// Digital circuit Computing_Sistem.dig as structural Verilog
module Computing_Sistem (
);

  wire _8registers_encoded_1_p1, _8registers_encoded_1_p2, _8registers_encoded_1_p3,
       _8registers_encoded_1_p4, _8registers_encoded_1_p5, _8registers_encoded_1_p6,
       _8registers_encoded_1_p7, _8registers_encoded_1_p8, _8registers_encoded_1_p9,
       _8registers_encoded_1_p10, _8registers_encoded_1_p11, _8registers_encoded_1_p12,
       _8registers_encoded_1_p13, _8registers_encoded_1_p14, _8registers_encoded_1_p15,
       _8registers_encoded_1_p16, _16bit_register_1_p1, _16bit_register_1_p2, ALU_p1, ALU_p2, ALU_p3, ALU_p4,
       ALU_p5, ALU_p6, ALU_p7, ALU_p8, ALU_p9, ALU_p10, ALU_p11, ALU_p12, ALU_p13, ALU_p14,
       demultiplexer_1_out_0, demultiplexer_1_out_1, demultiplexer_2_out_0, demultiplexer_2_out_1,
       demultiplexer_3_out_0, demultiplexer_3_out_1, demultiplexer_4_out_0, demultiplexer_4_out_1,
       demultiplexer_5_out_0, demultiplexer_5_out_1, demultiplexer_6_out_0, demultiplexer_6_out_1,
       demultiplexer_7_out_0, demultiplexer_7_out_1, demultiplexer_8_out_0, demultiplexer_8_out_1,
       demultiplexer_9_out_0, demultiplexer_9_out_1, demultiplexer_10_out_0, demultiplexer_10_out_1,
       demultiplexer_11_out_0, demultiplexer_11_out_1, demultiplexer_12_out_0, demultiplexer_12_out_1,
       demultiplexer_13_out_0, demultiplexer_13_out_1, demultiplexer_14_out_0, demultiplexer_14_out_1,
       demultiplexer_15_out_0, demultiplexer_15_out_1, demultiplexer_16_out_0, demultiplexer_16_out_1,
       IR_q_0, IR_q_1, IR_q_2, IR_q_3, IR_q_4, IR_q_5, IR_q_6, IR_q_7, IR_q_8, IR_q_9, IR_q_10, IR_q_11,
       IR_q_12, IR_q_13, IR_q_14, IR_q_15, IR_q_16, IR_q_17, IR_q_18, IR_q_19, IR_q_20, IR_q_21,
       Memory_outdata_0, Memory_outdata_1, Memory_outdata_2, Memory_outdata_3, Memory_outdata_4,
       Memory_outdata_5, Memory_outdata_6, Memory_outdata_7, Memory_outdata_8, Memory_outdata_9,
       Memory_outdata_10, Memory_outdata_11, Memory_outdata_12, Memory_outdata_13, Memory_outdata_14,
       Memory_outdata_15, multiplexer_1_out, multiplexer_2_out, multiplexer_3_out, multiplexer_4_out,
       multiplexer_5_out, multiplexer_6_out, multiplexer_7_out, multiplexer_8_out, multiplexer_9_out,
       multiplexer_10_out, multiplexer_11_out, multiplexer_12_out, multiplexer_13_out, multiplexer_14_out,
       multiplexer_15_out, multiplexer_16_out, or_1_out, PC_p1, PC_p2, PC_p3, PC_p4, PC_p5, PC_p6, PC_p7,
       PC_p8, PC_p9, PC_p10, PC_p11, PC_p12, PC_p13, PC_p14, PC_p15, PC_p16, undriven, undriven_2,
       undriven_3, undriven_4;

  // Program_Counter PC: pin names not known; wires that end beside it: PC_p1, PC_p2, PC_p3, PC_p4, PC_p5, PC_p6, PC_p7, PC_p8, PC_p9, PC_p10, PC_p11, PC_p12, PC_p13, PC_p14, PC_p15, PC_p16
  or or_1 (or_1_out, undriven_4, undriven_3, undriven_2, undriven);
  Memory IR (
    .A_0(PC_p1), .A_1(PC_p2), .A_2(PC_p3), .A_3(PC_p4), .A_4(PC_p5), .A_5(PC_p6), .A_6(PC_p7), .A_7(PC_p8),
    .A_8(PC_p9), .A_9(PC_p10), .A_10(PC_p11), .A_11(PC_p12), .A_12(PC_p13), .A_13(PC_p14), .A_14(PC_p15),
    .A_15(PC_p16), .Q_7(IR_q_7), .Q_6(IR_q_6), .Q_5(IR_q_5), .Q_4(IR_q_4), .Q_3(IR_q_3), .Q_0(IR_q_0),
    .Q_1(IR_q_1), .Q_2(IR_q_2), .Q_15(IR_q_15), .Q_14(IR_q_14), .Q_13(IR_q_13), .Q_12(IR_q_12),
    .Q_11(IR_q_11), .Q_8(IR_q_8), .Q_9(IR_q_9), .Q_10(IR_q_10), .Q_21(IR_q_21), .Q_20(IR_q_20),
    .Q_19(IR_q_19), .Q_18(IR_q_18), .Q_16(IR_q_16), .Q_17(IR_q_17));
  Semafor semafor_1 ();  // open: Enable_counters, Reset_counters, Async_counter1, Async_counter2, Async_counter3, Flag_sensor1, Flag_sensor2, Flag_sensor3, Emergency_sensor, Set_verde, Set_galben, Set_rosu, Begin, Q_0_0, Q_0_1, Q_0_2, Q_0_3, Q_0_4, Q_0_5, Q_0_6, Q_0_7, Q_1_0, Q_1_1, Q_1_2, Q_1_3, Q_1_4, Q_1_5, Q_1_6, Q_1_7, Q_2_0, Q_2_1, Q_2_2, Q_2_3, Q_2_4, Q_2_5, Q_2_6, Q_2_7, Flag_1, Flag_2, Flag_3, Emergency, Color_green, Color_yellow, Color_red
  Semafor semafor_2 ();  // open: Enable_counters, Reset_counters, Async_counter2, Async_counter3, Async_counter1, Flag_sensor1, Flag_sensor2, Flag_sensor3, Emergency_sensor, Set_verde, Set_galben, Set_rosu, Begin, Q_0_0, Q_0_1, Q_0_2, Q_0_3, Q_0_4, Q_0_5, Q_0_6, Q_0_7, Q_1_0, Q_1_1, Q_1_2, Q_1_3, Q_1_4, Q_1_5, Q_1_6, Q_1_7, Q_2_0, Q_2_1, Q_2_2, Q_2_3, Q_2_4, Q_2_5, Q_2_6, Q_2_7, Flag_1, Flag_2, Flag_3, Emergency, Color_green, Color_yellow, Color_red
  // _8Registers_encoded _8registers_encoded_1: pin names not known; wires that end beside it: _8registers_encoded_1_p1, _8registers_encoded_1_p2, _8registers_encoded_1_p3, _8registers_encoded_1_p4, _8registers_encoded_1_p5, _8registers_encoded_1_p6, _8registers_encoded_1_p7, _8registers_encoded_1_p8, _8registers_encoded_1_p9, _8registers_encoded_1_p10, _8registers_encoded_1_p11, _8registers_encoded_1_p12, _8registers_encoded_1_p13, _8registers_encoded_1_p14, _8registers_encoded_1_p15, _8registers_encoded_1_p16
  Semafor semafor_3 ();  // open: Enable_counters, Reset_counters, Async_counter2, Async_counter3, Async_counter1, Flag_sensor1, Flag_sensor2, Flag_sensor3, Emergency_sensor, Set_verde, Set_galben, Set_rosu, Begin, Q_0_0, Q_0_1, Q_0_2, Q_0_3, Q_0_4, Q_0_5, Q_0_6, Q_0_7, Q_1_0, Q_1_1, Q_1_2, Q_1_3, Q_1_4, Q_1_5, Q_1_6, Q_1_7, Q_2_0, Q_2_1, Q_2_2, Q_2_3, Q_2_4, Q_2_5, Q_2_6, Q_2_7, Flag_1, Flag_2, Flag_3, Emergency, Color_green, Color_yellow, Color_red
  Semafor semafor_4 ();  // open: Enable_counters, Reset_counters, Async_counter2, Async_counter3, Async_counter1, Flag_sensor1, Flag_sensor2, Flag_sensor3, Emergency_sensor, Set_verde, Set_galben, Set_rosu, Begin, Q_0_0, Q_0_1, Q_0_2, Q_0_3, Q_0_4, Q_0_5, Q_0_6, Q_0_7, Q_1_0, Q_1_1, Q_1_2, Q_1_3, Q_1_4, Q_1_5, Q_1_6, Q_1_7, Q_2_0, Q_2_1, Q_2_2, Q_2_3, Q_2_4, Q_2_5, Q_2_6, Q_2_7, Flag_1, Flag_2, Flag_3, Emergency, Color_green, Color_yellow, Color_red
  // ALU ALU: pin names not known; wires that end beside it: ALU_p1, ALU_p2, ALU_p3, ALU_p4, ALU_p5, ALU_p6, ALU_p7, ALU_p8, ALU_p9, ALU_p10, ALU_p11, ALU_p12, ALU_p13, ALU_p14
  // _16bit_register _16bit_register_1: pin names not known; wires that end beside it: _16bit_register_1_p1, _16bit_register_1_p2, ALU_p14, ALU_p13, ALU_p12, ALU_p11, ALU_p10, ALU_p9, ALU_p8, ALU_p7, ALU_p6, ALU_p5, ALU_p4, ALU_p3, ALU_p2, ALU_p1
  Demultiplexer demultiplexer_1 (
    .in(ALU_p1), .out_0(demultiplexer_1_out_0), .out_1(demultiplexer_1_out_1));  // open: sel
  Demultiplexer demultiplexer_2 (
    .in(ALU_p2), .out_0(demultiplexer_2_out_0), .out_1(demultiplexer_2_out_1));  // open: sel
  Demultiplexer demultiplexer_3 (
    .in(ALU_p3), .out_0(demultiplexer_3_out_0), .out_1(demultiplexer_3_out_1));  // open: sel
  Demultiplexer demultiplexer_4 (
    .in(ALU_p4), .out_0(demultiplexer_4_out_0), .out_1(demultiplexer_4_out_1));  // open: sel
  Demultiplexer demultiplexer_5 (
    .in(ALU_p5), .out_0(demultiplexer_5_out_0), .out_1(demultiplexer_5_out_1));  // open: sel
  Demultiplexer demultiplexer_6 (
    .in(ALU_p6), .out_0(demultiplexer_6_out_0), .out_1(demultiplexer_6_out_1));  // open: sel
  Demultiplexer demultiplexer_7 (
    .in(ALU_p7), .out_0(demultiplexer_7_out_0), .out_1(demultiplexer_7_out_1));  // open: sel
  Demultiplexer demultiplexer_8 (
    .in(ALU_p8), .out_0(demultiplexer_8_out_0), .out_1(demultiplexer_8_out_1));  // open: sel
  Demultiplexer demultiplexer_9 (
    .in(ALU_p9), .out_0(demultiplexer_9_out_0), .out_1(demultiplexer_9_out_1));  // open: sel
  Demultiplexer demultiplexer_10 (
    .in(ALU_p10), .out_0(demultiplexer_10_out_0), .out_1(demultiplexer_10_out_1));  // open: sel
  Demultiplexer demultiplexer_11 (
    .in(ALU_p11), .out_0(demultiplexer_11_out_0), .out_1(demultiplexer_11_out_1));  // open: sel
  Demultiplexer demultiplexer_12 (
    .in(ALU_p12), .out_0(demultiplexer_12_out_0), .out_1(demultiplexer_12_out_1));  // open: sel
  Demultiplexer demultiplexer_13 (
    .in(ALU_p13), .out_0(demultiplexer_13_out_0), .out_1(demultiplexer_13_out_1));  // open: sel
  Demultiplexer demultiplexer_14 (
    .in(ALU_p14), .out_0(demultiplexer_14_out_0), .out_1(demultiplexer_14_out_1));  // open: sel
  Demultiplexer demultiplexer_15 (
    .in(_16bit_register_1_p2), .out_0(demultiplexer_15_out_0), .out_1(demultiplexer_15_out_1));  // open: sel
  Demultiplexer demultiplexer_16 (
    .in(_16bit_register_1_p1), .out_0(demultiplexer_16_out_0), .out_1(demultiplexer_16_out_1));  // open: sel
  Multiplexer multiplexer_1 (
    .in_0(demultiplexer_1_out_1), .in_1(_8registers_encoded_1_p1), .out(multiplexer_1_out));  // open: sel
  Multiplexer multiplexer_2 (
    .in_0(demultiplexer_2_out_1), .in_1(_8registers_encoded_1_p2), .out(multiplexer_2_out));  // open: sel
  Multiplexer multiplexer_3 (
    .in_0(demultiplexer_3_out_1), .in_1(_8registers_encoded_1_p3), .out(multiplexer_3_out));  // open: sel
  Multiplexer multiplexer_4 (
    .in_0(demultiplexer_4_out_1), .in_1(_8registers_encoded_1_p4), .out(multiplexer_4_out));  // open: sel
  Multiplexer multiplexer_5 (
    .in_0(demultiplexer_5_out_1), .in_1(_8registers_encoded_1_p5), .out(multiplexer_5_out));  // open: sel
  Multiplexer multiplexer_6 (
    .in_0(demultiplexer_6_out_1), .in_1(_8registers_encoded_1_p6), .out(multiplexer_6_out));  // open: sel
  Multiplexer multiplexer_7 (
    .in_0(demultiplexer_7_out_1), .in_1(_8registers_encoded_1_p7), .out(multiplexer_7_out));  // open: sel
  Multiplexer multiplexer_8 (
    .in_0(demultiplexer_8_out_1), .in_1(_8registers_encoded_1_p8), .out(multiplexer_8_out));  // open: sel
  Multiplexer multiplexer_9 (
    .in_0(demultiplexer_9_out_1), .in_1(_8registers_encoded_1_p9), .out(multiplexer_9_out));  // open: sel
  Multiplexer multiplexer_10 (
    .in_0(demultiplexer_10_out_1), .in_1(_8registers_encoded_1_p10), .out(multiplexer_10_out));  // open: sel
  Multiplexer multiplexer_11 (
    .in_0(demultiplexer_11_out_1), .in_1(_8registers_encoded_1_p11), .out(multiplexer_11_out));  // open: sel
  Multiplexer multiplexer_12 (
    .in_0(demultiplexer_12_out_1), .in_1(_8registers_encoded_1_p12), .out(multiplexer_12_out));  // open: sel
  Multiplexer multiplexer_13 (
    .in_0(demultiplexer_13_out_1), .in_1(_8registers_encoded_1_p13), .out(multiplexer_13_out));  // open: sel
  Multiplexer multiplexer_14 (
    .in_0(demultiplexer_14_out_1), .in_1(_8registers_encoded_1_p14), .out(multiplexer_14_out));  // open: sel
  Multiplexer multiplexer_15 (
    .in_0(demultiplexer_15_out_1), .in_1(_8registers_encoded_1_p15), .out(multiplexer_15_out));  // open: sel
  Multiplexer multiplexer_16 (
    .in_0(demultiplexer_16_out_1), .in_1(_8registers_encoded_1_p16), .out(multiplexer_16_out));  // open: sel
  DataMemory Memory (
    .A_0(demultiplexer_1_out_0), .A_1(demultiplexer_2_out_0), .A_2(demultiplexer_3_out_0),
    .A_3(demultiplexer_4_out_0), .A_4(demultiplexer_5_out_0), .A_5(demultiplexer_6_out_0),
    .A_6(demultiplexer_7_out_0), .A_7(demultiplexer_8_out_0), .A_8(demultiplexer_9_out_0),
    .A_9(demultiplexer_10_out_0), .A_10(demultiplexer_11_out_0), .A_11(demultiplexer_12_out_0),
    .A_12(demultiplexer_13_out_0), .A_13(demultiplexer_14_out_0), .A_14(demultiplexer_15_out_0),
    .A_15(demultiplexer_16_out_0), .D_0(multiplexer_1_out), .D_1(multiplexer_2_out), .D_2(multiplexer_3_out),
    .D_3(multiplexer_4_out), .D_4(multiplexer_5_out), .D_5(multiplexer_6_out), .D_6(multiplexer_7_out),
    .D_7(multiplexer_8_out), .D_8(multiplexer_9_out), .D_9(multiplexer_10_out), .D_10(multiplexer_11_out),
    .D_11(multiplexer_12_out), .D_12(multiplexer_13_out), .D_13(multiplexer_14_out),
    .D_14(multiplexer_15_out), .D_15(multiplexer_16_out), .OutData_0(Memory_outdata_0),
    .OutData_1(Memory_outdata_1), .OutData_2(Memory_outdata_2), .OutData_3(Memory_outdata_3),
    .OutData_4(Memory_outdata_4), .OutData_5(Memory_outdata_5), .OutData_6(Memory_outdata_6),
    .OutData_7(Memory_outdata_7), .OutData_8(Memory_outdata_8), .OutData_9(Memory_outdata_9),
    .OutData_10(Memory_outdata_10), .OutData_11(Memory_outdata_11), .OutData_12(Memory_outdata_12),
    .OutData_13(Memory_outdata_13), .OutData_14(Memory_outdata_14), .OutData_15(Memory_outdata_15));  // open: WE
  _16bit_mux_2to1 WB (
    .I0_0(ALU_p1), .I0_1(ALU_p2), .I0_2(ALU_p3), .I0_3(ALU_p4), .I0_4(ALU_p5), .I0_5(ALU_p6), .I0_6(ALU_p7),
    .I0_7(ALU_p8), .I0_8(ALU_p9), .I0_9(ALU_p10), .I0_10(ALU_p11), .I0_11(ALU_p12), .I0_12(ALU_p13),
    .I0_13(ALU_p14), .I0_14(_16bit_register_1_p2), .I0_15(_16bit_register_1_p1), .I1_0(Memory_outdata_0),
    .I1_1(Memory_outdata_1), .I1_2(Memory_outdata_2), .I1_3(Memory_outdata_3), .I1_4(Memory_outdata_4),
    .I1_5(Memory_outdata_5), .I1_6(Memory_outdata_6), .I1_7(Memory_outdata_7), .I1_8(Memory_outdata_8),
    .I1_9(Memory_outdata_9), .I1_10(Memory_outdata_10), .I1_11(Memory_outdata_11), .I1_12(Memory_outdata_12),
    .I1_13(Memory_outdata_13), .I1_14(Memory_outdata_14), .I1_15(Memory_outdata_15));  // open: Select, Output_0, Output_1, Output_2, Output_3, Output_4, Output_5, Output_6, Output_7, Output_8, Output_9, Output_10, Output_11, Output_12, Output_13, Output_14, Output_15

  // Notes on the sheet:
  //   exp
  //   CS bits
  //   BA bits
  //   CF bits
endmodule
